// Logisim project fib.circ as structural Verilog: 6 circuits, main circuit main
module main (
  input  [2:0] in_1,
  output [3:0] \output 
);

  wire [1:0] mux_select_pin_1_out_2;
  wire [3:0] cal_1_out_2;

  cal cal_1 (.in_1(in_1), .out_2(cal_1_out_2));
  mux_select_pin mux_select_pin_1 (.in_1(in_1), .out_2(mux_select_pin_1_out_2));
  Multiplexer #(.select(2), .width(4)) multiplexer_1 (
    .in0(4'b0000), .in1(4'b0001), .in2(4'b0001), .in3(cal_1_out_2), .out(\output ),
    .sel(mux_select_pin_1_out_2));  // open: en

  // Other names for the same wires on the sheet: input[2:0] = in_1
endmodule

module init_reg (
  input  [3:0] init,
  input  [3:0] \input ,
  input  rst,
  output [3:0] out_4
);

  wire clock_1_out;
  wire [3:0] register_1_q, xor_1_out;

  assign xor_1_out = init ^ \input ;  // XOR_Gate xor_1, 4 bits wide
  Register #(.width(4)) register_1 (.D(xor_1_out), .Q(register_1_q), .clk(clock_1_out), .clr(rst));  // open: en
  Clock clock_1 (.out(clock_1_out));
  assign out_4 = init ^ register_1_q;  // XOR_Gate xor_2, 4 bits wide
endmodule

module is_equal (
  input  [2:0] in_1,
  input  [2:0] in_2,
  output out_3
);

  Comparator #(.width(3)) comparator_1 (.a(in_1), .b(in_2), .eq(out_3));  // open: gt, lt
endmodule

module mux_select_pin (
  input  [2:0] in_1,
  output [1:0] out_2
);

  or or_1 (out_2[1], in_1[1], in_1[2]);
  or or_2 (out_2[0], in_1[0], in_1[2]);

  // Other names for the same wires on the sheet: s2 = in_1[0]; s1 = in_1[1]; s0 = in_1[2]
endmodule

module cal (
  input  [2:0] in_1,
  output [3:0] out_2
);

  wire and_1_out, clk, clock_2_out, comparator_1_eq, counter_1_carry, is_equal_1_out_3, not_2_out,
       once_reg_1_out_3, rst;
  wire [2:0] counter_1_q, register_1_q, subtractor_1_out;
  wire [3:0] F_n, F_n_1, F_n_2, multiplexer_1_out;

  Clock clock_1 (.out(clk));
  Comparator #(.width(3)) comparator_1 (.a(subtractor_1_out), .b(register_1_q), .eq(comparator_1_eq));  // open: gt, lt
  not not_1 (rst, comparator_1_eq);
  Subtractor #(.width(3)) subtractor_1 (.a(in_1), .b(3'b011), .out(subtractor_1_out));  // open: bin, bout
  Register #(.width(3)) register_1 (.D(subtractor_1_out), .en(rst), .Q(register_1_q), .clk(clk));  // open: clr
  // Probe on F_n_2
  init_reg init_reg_1 (.init(4'b0001), .\input (F_n_1), .rst(rst), .out_4(F_n_2));
  Counter #(.width(3), .max('h7)) counter_1 (
    .load(1'b0), .count(1'b1), .Q(counter_1_q), .carry(counter_1_carry), .clk(clk), .clr(rst));  // open: D
  // Probe on F_n
  Adder #(.width(4)) adder_1 (.a(F_n_2), .b(F_n_1), .out(F_n));  // open: cin, cout
  is_equal is_equal_1 (.in_1(counter_1_q), .in_2(subtractor_1_out), .out_3(is_equal_1_out_3));
  once_reg once_reg_1 (.in_1(counter_1_carry), .rst(rst), .out_3(once_reg_1_out_3));
  not not_2 (not_2_out, once_reg_1_out_3);
  Multiplexer #(.width(4)) multiplexer_1 (
    .in0(4'b0000), .in1(F_n), .out(multiplexer_1_out), .sel(and_1_out));  // open: en
  // Probe on multiplexer_1_out
  and and_1 (and_1_out, is_equal_1_out_3, not_2_out);
  // Probe on F_n_1
  init_reg init_reg_2 (.init(4'b0001), .\input (F_n), .rst(rst), .out_4(F_n_1));
  Register #(.width(4)) register_2 (.D(multiplexer_1_out), .en(and_1_out), .Q(out_2), .clk(clock_2_out), .clr(rst));
  Clock clock_2 (.out(clock_2_out));

  // Other names for the same wires on the sheet: input[2:0] = in_1
endmodule

module once_reg (
  input  in_1,
  input  rst,
  output out_3
);

  wire clock_1_out, not_1_out;

  not not_1 (not_1_out, out_3);
  Clock clock_1 (.out(clock_1_out));
  Register #(.width(1)) register_1 (.D(in_1), .en(not_1_out), .Q(out_3), .clk(clock_1_out), .clr(rst));
endmodule
