// Logisim project mod5.circ as structural Verilog: 3 circuits, main circuit mod5
module mod5 (
  input  in_1,
  output out_2,
  output out_3,
  output out_4,
  output out_5,
  output out_6
);

  wire clock_1_out;
  wire [1:0] State, state_tran_1_newlow;

  state_tran state_tran_1 (
    .high(State[1]), .low(State[0]), .\input (in_1), .newhigh(state_tran_1_newlow[1]),
    .newlow(state_tran_1_newlow[0]));
  Register #(.width(2)) register_1 (.D(state_tran_1_newlow), .Q(State), .clk(clock_1_out));  // open: en, clr
  Clock clock_1 (.out(clock_1_out));
  \output  output_1 (
    .high(State[1]), .low(State[0]), .\input (in_1), .S0(out_2), .S1(out_3), .S2(out_4), .S3(out_5),
    .S4(out_6));
endmodule

module state_tran (
  input  high,
  input  low,
  input  \input ,
  output newhigh,
  output newlow
);

  wire and_1_out, and_2_out, and_3_out, and_4_out, and_5_out, and_6_out, not_1_out, not_2_out, not_3_out,
       not_4_out, not_5_out, not_6_out, not_7_out, not_8_out;

  not not_1 (not_1_out, high);
  not not_2 (not_2_out, low);
  not not_3 (not_3_out, high);
  not not_4 (not_4_out, low);
  not not_5 (not_5_out, high);
  not not_6 (not_6_out, \input );
  not not_7 (not_7_out, low);
  not not_8 (not_8_out, \input );
  and and_1 (and_1_out, not_1_out, low);
  and and_2 (and_2_out, high, not_2_out);
  and and_3 (and_3_out, not_3_out, not_4_out, \input );
  and and_4 (and_4_out, not_5_out, low, not_6_out);
  and and_5 (and_5_out, high, not_7_out, not_8_out);
  and and_6 (and_6_out, high, low, \input );
  or or_1 (newhigh, and_1_out, and_2_out);
  or or_2 (newlow, and_3_out, and_4_out, and_5_out, and_6_out);
endmodule

module \output  (
  input  high,
  input  low,
  input  \input ,
  output S0,
  output S1,
  output S2,
  output S3,
  output S4
);

  wire and_1_out, and_2_out, and_3_out, and_4_out, and_5_out, and_6_out, and_7_out, and_8_out, not_1_out,
       not_2_out, not_3_out, not_4_out, not_5_out, not_6_out, not_7_out, not_8_out, not_9_out, not_10_out,
       not_11_out, not_12_out;

  not not_1 (not_1_out, high);
  not not_2 (not_2_out, low);
  not not_3 (not_3_out, \input );
  not not_4 (not_4_out, \input );
  not not_5 (not_5_out, high);
  not not_6 (not_6_out, low);
  not not_7 (not_7_out, high);
  not not_8 (not_8_out, low);
  not not_9 (not_9_out, high);
  not not_10 (not_10_out, \input );
  not not_11 (not_11_out, low);
  not not_12 (not_12_out, \input );
  and and_1 (and_1_out, not_1_out, not_2_out, not_3_out);
  and and_2 (and_2_out, high, low, not_4_out);
  and and_3 (and_3_out, not_5_out, not_6_out, \input );
  and and_4 (and_4_out, high, low, \input );
  and and_5 (and_5_out, not_7_out, low, \input );
  and and_6 (and_6_out, high, not_8_out, \input );
  and and_7 (and_7_out, not_9_out, low, not_10_out);
  and and_8 (and_8_out, high, not_11_out, not_12_out);
  or or_1 (S1, and_1_out, and_2_out);
  or or_2 (S2, and_3_out, and_4_out);
  or or_3 (S3, and_5_out, and_6_out);
  or or_4 (S4, and_7_out, and_8_out);

  assign S0 = 1'b0;
endmodule
