// Logisim project sort.circ as structural Verilog
module _1bit_swap (
  input  A,
  input  B,
  input  C,
  output o1,
  output o2
);

  wire and_1_out, and_2_out, and_3_out, and_4_out, not_1_out, not_2_out;

  not not_1 (not_1_out, C);
  not not_2 (not_2_out, C);
  and and_1 (and_1_out, B, C);
  and and_2 (and_2_out, A, not_1_out);
  and and_3 (and_3_out, B, not_2_out);
  and and_4 (and_4_out, A, C);
  or or_1 (o1, and_1_out, and_2_out);
  or or_2 (o2, and_3_out, and_4_out);
endmodule

module _4bit_swap (
  input  [3:0] A,
  input  [3:0] B,
  input  S,
  output [3:0] O1,
  output [3:0] O2
);

  _1bit_swap u_1bit_swap_1 (.A(A[0]), .B(B[0]), .C(S), .o1(O1[0]), .o2(O2[0]));
  _1bit_swap u_1bit_swap_2 (.A(A[1]), .B(B[1]), .C(S), .o1(O1[1]), .o2(O2[1]));
  _1bit_swap u_1bit_swap_3 (.A(A[2]), .B(B[2]), .C(S), .o1(O1[2]), .o2(O2[2]));
  _1bit_swap u_1bit_swap_4 (.A(A[3]), .B(B[3]), .C(S), .o1(O1[3]), .o2(O2[3]));
endmodule

module compare (
  input  [3:0] in_1,
  input  [3:0] in_2,
  output [3:0] out_3,
  output [3:0] out_4
);

  wire comparator_1_gt;

  Comparator #(.width(4), .mode("unsigned")) comparator_1 (.a(in_1), .b(in_2), .gt(comparator_1_gt));  // open: eq, lt
  _4bit_swap u_4bit_swap_1 (.A(in_1), .B(in_2), .S(comparator_1_gt), .O1(out_3), .O2(out_4));
endmodule

module _4bit_sort (
  input  [3:0] in_1,
  input  [3:0] in_2,
  input  [3:0] in_3,
  input  [3:0] in_4,
  output [3:0] out_5,
  output [3:0] out_6,
  output [3:0] out_7,
  output [3:0] out_8
);

  wire [3:0] compare_1_out_3, compare_1_out_4, compare_2_out_3, compare_2_out_4, compare_3_out_3,
       compare_4_out_3, compare_4_out_4, compare_5_out_3;

  compare compare_1 (.in_1(in_1), .in_2(in_2), .out_3(compare_1_out_3), .out_4(compare_1_out_4));
  compare compare_2 (.in_1(compare_1_out_4), .in_2(in_3), .out_3(compare_2_out_3), .out_4(compare_2_out_4));
  compare compare_3 (.in_1(compare_2_out_4), .in_2(in_4), .out_3(compare_3_out_3), .out_4(out_8));
  compare compare_4 (.in_1(compare_1_out_3), .in_2(compare_2_out_3), .out_3(compare_4_out_3), .out_4(compare_4_out_4));
  compare compare_5 (.in_1(compare_4_out_4), .in_2(compare_3_out_3), .out_3(compare_5_out_3), .out_4(out_7));
  compare compare_6 (.in_1(compare_4_out_3), .in_2(compare_5_out_3), .out_3(out_5), .out_4(out_6));
endmodule
