// Logisim project swap.circ as structural Verilog: 1 circuit, main circuit swap
module swap (
  input  I1,
  input  I2,
  input  S,
  output O1,
  output O2
);

  wire and_1_out, and_2_out, and_3_out, and_4_out, and_5_out, and_6_out, and_7_out, and_8_out, not_1_out,
       not_2_out, not_3_out;

  not not_1 (not_1_out, I1);
  not not_2 (not_2_out, I2);
  not not_3 (not_3_out, S);
  and and_1 (and_1_out, S, not_1_out, I2);
  and and_2 (and_2_out, S, I1, I2);
  and and_3 (and_3_out, S, I1, not_2_out);
  and and_4 (and_4_out, S, I1, I2);
  and and_5 (and_5_out, not_3_out, I1, I2);
  and and_6 (and_6_out, not_3_out, I1, not_2_out);
  and and_7 (and_7_out, not_3_out, I1, I2);
  and and_8 (and_8_out, not_3_out, not_1_out, I2);
  or or_1 (O1, and_1_out, and_2_out, and_5_out, and_6_out);
  or or_2 (O2, and_7_out, and_8_out, and_3_out, and_4_out);
endmodule
