// Logisim project crc.circ as structural Verilog: 2 circuits, main circuit CRC
module CRC (
  input  [7:0] in_1,
  input  [3:0] in_2,
  output [10:0] out_3
);

  wire [2:0] mod2_4bits_1_remainder, mod2_4bits_2_remainder, mod2_4bits_3_remainder, mod2_4bits_4_remainder,
       mod2_4bits_5_remainder, mod2_4bits_6_remainder, mod2_4bits_7_remainder;

  mod2_4bits mod2_4bits_1 (.dividend(in_1[7:4]), .divisor(in_2), .remainder(mod2_4bits_1_remainder));  // open: quotient
  mod2_4bits mod2_4bits_2 (
    .dividend({mod2_4bits_1_remainder, in_1[3]}), .divisor(in_2), .remainder(mod2_4bits_2_remainder));  // open: quotient
  mod2_4bits mod2_4bits_3 (
    .dividend({mod2_4bits_2_remainder, in_1[2]}), .divisor(in_2), .remainder(mod2_4bits_3_remainder));  // open: quotient
  mod2_4bits mod2_4bits_4 (
    .dividend({mod2_4bits_3_remainder, in_1[1]}), .divisor(in_2), .remainder(mod2_4bits_4_remainder));  // open: quotient
  mod2_4bits mod2_4bits_5 (
    .dividend({mod2_4bits_4_remainder, in_1[0]}), .divisor(in_2), .remainder(mod2_4bits_5_remainder));  // open: quotient
  mod2_4bits mod2_4bits_6 (
    .dividend({mod2_4bits_5_remainder, 1'b0}), .divisor(in_2), .remainder(mod2_4bits_6_remainder));  // open: quotient
  mod2_4bits mod2_4bits_7 (
    .dividend({mod2_4bits_6_remainder, 1'b0}), .divisor(in_2), .remainder(mod2_4bits_7_remainder));  // open: quotient
  mod2_4bits mod2_4bits_8 (
    .dividend({mod2_4bits_7_remainder, 1'b0}), .divisor(in_2), .remainder(out_3[2:0]));  // open: quotient

  assign out_3[10:3] = in_1;

  // Other names for the same wires on the sheet: divd[10:3] = in_1; input[7:0] = in_1; div[3:0] = in_2;
  //   remain[2:0] = out_3[2:0]
endmodule

module mod2_4bits (
  input  [3:0] dividend,
  input  [3:0] divisor,
  output [2:0] remainder,
  output quotient
);

  wire [3:0] xor_1_out;
  wire [3:3] multiplexer_2_out;

  Multiplexer multiplexer_1 (.in0(1'b0), .in1(1'b1), .out(quotient), .sel(dividend[3]));  // open: en
  assign xor_1_out = dividend ^ divisor;  // XOR_Gate xor_1, 4 bits wide
  Multiplexer #(.width(4)) multiplexer_2 (
    .in0(dividend), .in1(xor_1_out), .out({multiplexer_2_out[3], remainder}), .sel(dividend[3]));  // open: en

  // Other names for the same wires on the sheet: highbit = dividend[3]
endmodule
