// Logisim project elevator.circ as structural Verilog: 3 circuits, main circuit main
module main (
  input  [3:0] in_1,
  input  [7:0] in_2,
  input  [7:0] in_3,
  input  [7:0] in_4,
  input  [7:0] in_5,
  output [7:0] out_6
);

  wire [7:0] from0, from1, from2, from3;

  sub1 sub1_1 (.in_1(in_3), .in_2(in_4), .in_3(in_5), .out_4(from0));
  sub2 sub2_1 (.in_1(in_2), .in_2(in_4), .in_3(in_5), .out_4(from1));
  sub2 sub2_2 (.in_1(in_5), .in_2(in_3), .in_3(in_2), .out_4(from2));
  sub1 sub1_2 (.in_1(in_4), .in_2(in_3), .in_3(in_2), .out_4(from3));
  Multiplexer #(.select(4), .width(8)) multiplexer_1 (
    .in1(from0), .in2(from1), .in4(from2), .in8(from3), .out(out_6), .sel(in_1));  // open: in0, in3, in5, in6, in7, in9, in10, in11, in12, in13, in14, in15, en

  // Other names for the same wires on the sheet: _0[7:0] = in_2; _1[7:0] = in_3; _2[7:0] = in_4; _3[7:0] = in_5;
  //   from[3:0] = in_1
endmodule

module sub1 (
  input  [7:0] in_1,
  input  [7:0] in_2,
  input  [7:0] in_3,
  output [7:0] out_4
);

  wire [2:0] comp;

  Comparator #(.mode("unsigned")) comparator_1 (.a(in_1), .b(in_2), .gt(comp[0]));  // open: eq, lt
  Comparator #(.mode("unsigned")) comparator_2 (.a(in_1), .b(in_3), .gt(comp[1]));  // open: eq, lt
  Comparator #(.mode("unsigned")) comparator_3 (.a(in_2), .b(in_3), .gt(comp[2]));  // open: eq, lt
  Multiplexer #(.select(3), .width(8)) multiplexer_1 (
    .in0(8'h5), .in1(8'h6), .in3(8'h4), .in4(8'h5), .in6(8'h5), .in7(8'h3), .out(out_4), .sel(comp));  // open: in2, in5, en
endmodule

module sub2 (
  input  [7:0] in_1,
  input  [7:0] in_2,
  input  [7:0] in_3,
  output [7:0] out_4
);

  wire [2:0] comp;

  Comparator #(.mode("unsigned")) comparator_1 (.a(in_1), .b(in_2), .gt(comp[0]));  // open: eq, lt
  Comparator #(.mode("unsigned")) comparator_2 (.a(in_1), .b(in_3), .gt(comp[1]));  // open: eq, lt
  Comparator #(.mode("unsigned")) comparator_3 (.a(in_2), .b(in_3), .gt(comp[2]));  // open: eq, lt
  Multiplexer #(.select(3), .width(8)) multiplexer_1 (
    .in0(8'h5), .in1(8'h7), .in3(8'h5), .in4(8'h5), .in6(8'h6), .in7(8'h4), .out(out_4), .sel(comp));  // open: in2, in5, en
endmodule
