// Logisim project fsm.circ as structural Verilog: 3 circuits, main circuit fsm
module fsm (
  input  CLR,
  input  [1:0] in,
  output out_3
);

  wire clk;
  wire [1:0] multiplexer_1_out, next_state, trans_1_s0n;

  Clock clock_1 (.out(clk));
  trans trans_1 (
    .s1(next_state[1]), .s0(next_state[0]), .in1(in[1]), .in0(in[0]), .s1n(trans_1_s0n[1]),
    .s0n(trans_1_s0n[0]));
  Multiplexer #(.width(2), .enable("false")) multiplexer_1 (
    .in0(trans_1_s0n), .in1(2'b00), .out(multiplexer_1_out), .sel(CLR));
  Register #(.width(2)) register_1 (.D(multiplexer_1_out), .Q(next_state), .clk(clk));  // open: en, clr
  \output  output_1 (.s1(next_state[1]), .s0(next_state[0]), .in1(in[1]), .in0(in[0]), .z(out_3));
endmodule

module trans (
  input  s1,
  input  s0,
  input  in1,
  input  in0,
  output s1n,
  output s0n
);

  wire and_1_out, and_2_out, and_3_out, and_4_out, not_1_out, not_2_out, not_3_out, not_4_out, not_5_out,
       not_6_out, not_7_out;

  not not_1 (not_1_out, s1);
  and and_1 (and_1_out, not_1_out, s0, not_2_out);
  not not_2 (not_2_out, in0);
  and and_2 (and_2_out, s1, not_3_out, not_4_out);
  not not_3 (not_3_out, s0);
  not not_4 (not_4_out, in0);
  not not_5 (not_5_out, in1);
  and and_3 (and_3_out, not_5_out, in0);
  not not_6 (not_6_out, s0);
  and and_4 (and_4_out, s1, not_6_out, not_7_out);
  not not_7 (not_7_out, in0);
  or or_1 (s1n, and_1_out, and_2_out);
  or or_2 (s0n, and_3_out, and_4_out);
endmodule

module \output  (
  input  s1,
  input  s0,
  input  in1,
  input  in0,
  output z
);

  wire not_1_out, not_2_out;

  and and_1 (z, s1, not_1_out, not_2_out);
  not not_1 (not_1_out, s0);
  not not_2 (not_2_out, in0);
endmodule
