// Logisim project grf.circ as structural Verilog: 1 circuit, main circuit grf
module grf (
  input  clk,
  input  reset,
  input  WE,
  input  [4:0] A1,
  input  [4:0] A2,
  input  [4:0] A3,
  input  [31:0] WD,
  output [31:0] RD1,
  output [31:0] RD2
);

  wire [31:0] _0, _1, _2, _3, _4, _5, _6, _7, _8, _9, _10, _11, _12, _13, _14, _15, _16, _17, _18, _19, _20,
       _21, _22, _23, _24, _25, _26, _27, _28, _29, _30, _31, w0, w1, w2, w3, w4, w5, w6, w7, w8, w9, w10,
       w11, w12, w13, w14, w15, w16, w17, w18, w19, w20, w21, w22, w23, w24, w25, w26, w27, w28, w29, w30,
       w31;

  Demultiplexer #(.select(5), .width(32)) demultiplexer_1 (
    .out0(w0), .out1(w1), .out2(w2), .out3(w3), .out4(w4), .out5(w5), .out6(w6), .out7(w7), .out8(w8),
    .out9(w9), .out10(w10), .out11(w11), .out12(w12), .out13(w13), .out14(w14), .out15(w15), .out16(w16),
    .out17(w17), .out18(w18), .out19(w19), .out20(w20), .out21(w21), .out22(w22), .out23(w23), .out24(w24),
    .out25(w25), .out26(w26), .out27(w27), .out28(w28), .out29(w29), .out30(w30), .out31(w31), .in(WD),
    .sel(A3));  // open: en
  Register #(.width(32)) register_1 (.D(w0), .en(1'b0), .Q(_0), .clk(clk), .clr(reset));
  Register #(.width(32)) register_2 (.D(w1), .en(WE), .Q(_1), .clk(clk), .clr(reset));
  Register #(.width(32)) register_3 (.D(w2), .en(WE), .Q(_2), .clk(clk), .clr(reset));
  Register #(.width(32)) register_4 (.D(w3), .en(WE), .Q(_3), .clk(clk), .clr(reset));
  Register #(.width(32)) register_5 (.D(w4), .en(WE), .Q(_4), .clk(clk), .clr(reset));
  Register #(.width(32)) register_6 (.D(w5), .en(WE), .Q(_5), .clk(clk), .clr(reset));
  Register #(.width(32)) register_7 (.D(w6), .en(WE), .Q(_6), .clk(clk), .clr(reset));
  Register #(.width(32)) register_8 (.D(w7), .en(WE), .Q(_7), .clk(clk), .clr(reset));
  Multiplexer #(.select(5), .width(32)) multiplexer_1 (
    .in0(_0), .in1(_1), .in2(_2), .in3(_3), .in4(_4), .in5(_5), .in6(_6), .in7(_7), .in8(_8), .in9(_9),
    .in10(_10), .in11(_11), .in12(_12), .in13(_13), .in14(_14), .in15(_15), .in16(_16), .in17(_17),
    .in18(_18), .in19(_19), .in20(_20), .in21(_21), .in22(_22), .in23(_23), .in24(_24), .in25(_25),
    .in26(_26), .in27(_27), .in28(_28), .in29(_29), .in30(_30), .in31(_31), .out(RD1), .sel(A1));  // open: en
  Register #(.width(32)) register_9 (.D(w8), .en(WE), .Q(_8), .clk(clk), .clr(reset));
  Register #(.width(32)) register_10 (.D(w9), .en(WE), .Q(_9), .clk(clk), .clr(reset));
  Register #(.width(32)) register_11 (.D(w10), .en(WE), .Q(_10), .clk(clk), .clr(reset));
  Register #(.width(32)) register_12 (.D(w11), .en(WE), .Q(_11), .clk(clk), .clr(reset));
  Register #(.width(32)) register_13 (.D(w12), .en(WE), .Q(_12), .clk(clk), .clr(reset));
  Register #(.width(32)) register_14 (.D(w13), .en(WE), .Q(_13), .clk(clk), .clr(reset));
  Register #(.width(32)) register_15 (.D(w14), .en(WE), .Q(_14), .clk(clk), .clr(reset));
  Register #(.width(32)) register_16 (.D(w15), .en(WE), .Q(_15), .clk(clk), .clr(reset));
  Register #(.width(32)) register_17 (.D(w16), .en(WE), .Q(_16), .clk(clk), .clr(reset));
  Register #(.width(32)) register_18 (.D(w17), .en(WE), .Q(_17), .clk(clk), .clr(reset));
  Register #(.width(32)) register_19 (.D(w18), .en(WE), .Q(_18), .clk(clk), .clr(reset));
  Register #(.width(32)) register_20 (.D(w19), .en(WE), .Q(_19), .clk(clk), .clr(reset));
  Register #(.width(32)) register_21 (.D(w20), .en(WE), .Q(_20), .clk(clk), .clr(reset));
  Register #(.width(32)) register_22 (.D(w21), .en(WE), .Q(_21), .clk(clk), .clr(reset));
  Register #(.width(32)) register_23 (.D(w22), .en(WE), .Q(_22), .clk(clk), .clr(reset));
  Register #(.width(32)) register_24 (.D(w23), .en(WE), .Q(_23), .clk(clk), .clr(reset));
  Register #(.width(32)) register_25 (.D(w24), .en(WE), .Q(_24), .clk(clk), .clr(reset));
  Register #(.width(32)) register_26 (.D(w25), .en(WE), .Q(_25), .clk(clk), .clr(reset));
  Register #(.width(32)) register_27 (.D(w26), .en(WE), .Q(_26), .clk(clk), .clr(reset));
  Register #(.width(32)) register_28 (.D(w27), .en(WE), .Q(_27), .clk(clk), .clr(reset));
  Register #(.width(32)) register_29 (.D(w28), .en(WE), .Q(_28), .clk(clk), .clr(reset));
  Register #(.width(32)) register_30 (.D(w29), .en(WE), .Q(_29), .clk(clk), .clr(reset));
  Register #(.width(32)) register_31 (.D(w30), .en(WE), .Q(_30), .clk(clk), .clr(reset));
  Register #(.width(32)) register_32 (.D(w31), .en(WE), .Q(_31), .clk(clk), .clr(reset));
  Multiplexer #(.select(5), .width(32)) multiplexer_2 (
    .in0(_0), .in1(_1), .in2(_2), .in3(_3), .in4(_4), .in5(_5), .in6(_6), .in7(_7), .in8(_8), .in9(_9),
    .in10(_10), .in11(_11), .in12(_12), .in13(_13), .in14(_14), .in15(_15), .in16(_16), .in17(_17),
    .in18(_18), .in19(_19), .in20(_20), .in21(_21), .in22(_22), .in23(_23), .in24(_24), .in25(_25),
    .in26(_26), .in27(_27), .in28(_28), .in29(_29), .in30(_30), .in31(_31), .out(RD2), .sel(A2));  // open: en

  // Other names for the same wires on the sheet: rst = reset
endmodule
