// Logisim project navigation.circ as structural Verilog: 3 circuits, main circuit navigation
module navigation (
  input  [1:0] dir,
  input  clk,
  input  reset,
  output out_4,
  output out_5
);

  wire [3:0] next_status, trans_1_s0n;

  trans trans_1 (
    .s2(next_status[2]), .s1(next_status[1]), .s0(next_status[0]), .d1(dir[1]), .d0(dir[0]),
    .s2n(trans_1_s0n[2]), .s1n(trans_1_s0n[1]), .s0n(trans_1_s0n[0]), .hit(trans_1_s0n[3]));
  Register #(.width(4)) register_1 (.D(trans_1_s0n), .Q(next_status), .clk(clk), .clr(reset));  // open: en
  \output  output_1 (
    .s2(next_status[2]), .s1(next_status[1]), .s0(next_status[0]), .hit(next_status[3]), .arrive(out_4),
    .hit_2(out_5));

  // Other names for the same wires on the sheet: rst = reset
endmodule

module trans (
  input  s2,
  input  s1,
  input  s0,
  input  d1,
  input  d0,
  output s2n,
  output s1n,
  output s0n,
  output hit
);

  wire and_1_out, and_2_out, and_3_out, and_4_out, and_5_out, and_6_out, and_7_out, and_8_out, and_9_out,
       and_10_out, and_11_out, and_12_out, and_13_out, and_14_out, and_15_out, and_16_out, and_17_out,
       not_1_out, not_2_out, not_3_out, not_4_out, not_5_out, not_6_out, not_7_out, not_8_out, not_9_out,
       not_10_out, not_11_out, not_12_out, not_13_out, not_14_out, not_15_out, not_16_out, not_17_out,
       not_18_out, not_19_out, not_20_out, not_21_out, not_22_out, not_23_out, not_24_out, not_25_out,
       not_26_out, not_27_out, not_28_out, not_29_out, not_30_out, not_31_out, not_32_out, not_33_out;

  not not_1 (not_1_out, s0);
  not not_2 (not_2_out, d1);
  not not_3 (not_3_out, d1);
  not not_4 (not_4_out, d0);
  not not_5 (not_5_out, s1);
  not not_6 (not_6_out, d1);
  not not_7 (not_7_out, d1);
  not not_8 (not_8_out, s0);
  not not_9 (not_9_out, d1);
  not not_10 (not_10_out, d0);
  not not_11 (not_11_out, s0);
  not not_12 (not_12_out, d0);
  not not_13 (not_13_out, s2);
  not not_14 (not_14_out, s1);
  not not_15 (not_15_out, s0);
  not not_16 (not_16_out, d1);
  not not_17 (not_17_out, d0);
  not not_18 (not_18_out, d0);
  not not_19 (not_19_out, s2);
  not not_20 (not_20_out, s1);
  not not_21 (not_21_out, s0);
  not not_22 (not_22_out, s2);
  not not_23 (not_23_out, s1);
  not not_24 (not_24_out, s0);
  not not_25 (not_25_out, s2);
  not not_26 (not_26_out, s1);
  not not_27 (not_27_out, s2);
  not not_28 (not_28_out, s0);
  not not_29 (not_29_out, s0);
  not not_30 (not_30_out, d1);
  not not_31 (not_31_out, d0);
  not not_32 (not_32_out, d1);
  not not_33 (not_33_out, d0);
  and and_1 (and_1_out, s1, not_1_out, not_2_out, d0);
  and and_2 (and_2_out, s1, s0, not_3_out, not_4_out);
  and and_3 (and_3_out, not_5_out, s0, not_6_out);
  and and_4 (and_4_out, s0, not_7_out, d0);
  and and_5 (and_5_out, s1, not_8_out, not_9_out, not_10_out);
  and and_6 (and_6_out, s1, not_11_out, d1, d0);
  and and_7 (and_7_out, s1, s0, d1, not_12_out);
  and and_8 (and_8_out, not_13_out, not_14_out, not_15_out, not_16_out, not_17_out);
  and and_9 (and_9_out, s0, d0);
  and and_10 (and_10_out, s1, d1, not_18_out);
  and and_11 (and_11_out, not_19_out, not_20_out, not_21_out, d0);
  and and_12 (and_12_out, not_22_out, not_23_out, not_24_out, d1);
  and and_13 (and_13_out, not_25_out, not_26_out, d1, d0);
  and and_14 (and_14_out, not_27_out, not_28_out, d1, d0);
  and and_15 (and_15_out, s1, not_29_out, not_30_out, not_31_out);
  and and_16 (and_16_out, s1, s0, not_32_out, d0);
  and and_17 (and_17_out, s1, s0, d1, not_33_out);
  or or_1 (s2n, and_1_out, and_2_out);
  or or_2 (s1n, and_3_out, and_4_out, and_5_out, and_6_out, and_7_out);
  or or_3 (s0n, and_8_out, and_9_out, and_10_out);
  or or_4 (hit, and_11_out, and_12_out, and_13_out, and_14_out, and_15_out, and_16_out, and_17_out);
endmodule

module \output  (
  input  s2,
  input  s1,
  input  s0,
  input  hit,
  output arrive,
  output hit_2
);

  wire not_1_out, not_2_out;

  not not_1 (not_1_out, s1);
  not not_2 (not_2_out, s0);
  and and_1 (arrive, s2, not_1_out, not_2_out);

  assign hit_2 = hit;
endmodule
