// Logisim project cpu.circ as structural Verilog: 12 circuits, main circuit main
module main (
  input  in_1,
  output [31:0] out_2,
  output [31:0] out_3,
  output out_4,
  output [4:0] out_5,
  output [31:0] out_6,
  output out_7,
  output [31:0] out_8,
  output [31:0] out_9
);

  wire ALUInput1, ALUInput2, clk, Controller_RegWE, ExtOp, MemToReg, PCToReg, Reg_ra, RegDst, zero;
  wire [1:0] IFU_Sel;
  wire [4:0] multiplexer_1_out, \type ;
  wire [15:0] imm16;
  wire [25:0] imm26;
  wire [31:0] ALU_Data, bit_extender_2_out, bit_extender_3_out, bit_extender_4_out, DM_Data, GRF, GRF_Data2,
       immext_1_imm32, multiplexer_3_out, multiplexer_5_out, multiplexer_6_out, PC_4;

  Clock clock_1 (.out(clk));
  IFU ifu_1 (
    .GRF(GRF), .in_2(clk), .imm26(imm26), .imm16(imm16), .select(IFU_Sel), .zero(zero), .out_9(out_2),
    .in_3(in_1), .out_8(out_3), .out_10(PC_4));
  ImmExt immext_1 (.Instr(out_2), .Op(ExtOp), .imm32(immext_1_imm32), .imm16(imm16));
  Bit_Extender #(.in_width(32), .out_width(26)) bit_extender_1 (.in(out_2), .out(imm26));
  Multiplexer #(.width(5)) multiplexer_1 (
    .in0(out_2[15:11]), .in1(out_2[20:16]), .out(multiplexer_1_out), .sel(RegDst));  // open: en
  Multiplexer #(.width(5)) multiplexer_2 (
    .in0(multiplexer_1_out), .in1({5{1'b1}}), .out(out_5), .sel(Reg_ra));  // open: en
  Multiplexer #(.width(32)) multiplexer_3 (
    .in0(ALU_Data), .in1(DM_Data), .out(multiplexer_3_out), .sel(MemToReg));  // open: en
  Multiplexer #(.width(32)) multiplexer_4 (
    .in0(multiplexer_3_out), .in1(PC_4), .out(out_6), .sel(PCToReg));  // open: en
  assign bit_extender_2_out = {{27{1'b0}}, out_2[10:6]};  // Bit_Extender bit_extender_2
  GRF grf_1 (
    .A1(out_2[25:21]), .A2(out_2[20:16]), .A3(out_5), .WD(out_6), .RD1(GRF), .RD2(GRF_Data2), .clk(clk),
    .reset(in_1), .WE(out_4));
  RegWE regwe_1 (
    .in_1(Controller_RegWE), .in_3(out_2[20:16]), .in_4(out_2[15:11]), .in_5(out_2[10:6]), .in_6(\type ),
    .out_7(out_4), .in_2(out_2[25:21]));
  Controller controller_1 (
    .Funct(out_2[5:0]), .OpCode(out_2[31:26]), .nextPC_Sel(IFU_Sel), .\type (\type ),
    .RegWriteEnable(Controller_RegWE), .ALUInput2(ALUInput2), .ExtOp(ExtOp), .RegDst(RegDst), .DM_WE(out_7),
    .MemtoReg(MemToReg), .PCtoReg(PCToReg), .Reg_ra(Reg_ra), .ALUInput1(ALUInput1));
  Multiplexer #(.width(32)) multiplexer_5 (
    .in0(GRF), .in1(bit_extender_2_out), .out(multiplexer_5_out), .sel(ALUInput1));  // open: en
  Multiplexer #(.width(32)) multiplexer_6 (
    .in0(GRF_Data2), .in1(immext_1_imm32), .out(multiplexer_6_out), .sel(ALUInput2));  // open: en
  ALU alu_1 (.in1(multiplexer_5_out), .in2(multiplexer_6_out), .\type (\type ), .out(ALU_Data), .zero(zero));
  assign bit_extender_3_out = {{31{out_7}}, out_7};  // Bit_Extender bit_extender_3
  assign bit_extender_4_out = {{31{out_7}}, out_7};  // Bit_Extender bit_extender_4
  DM dm_1 (.Addr(ALU_Data), .WriteData(GRF_Data2), .WriteEnable(out_7), .clk(clk), .rst(in_1), .Data(DM_Data));
  assign out_9 = GRF_Data2 & bit_extender_3_out;  // AND_Gate and_1, 32 bits wide
  assign out_8 = ALU_Data & bit_extender_4_out;  // AND_Gate and_2, 32 bits wide

  // Other names for the same wires on the sheet: DMWE = out_7; Funct[5:0] = out_2[5:0]; Instr[31:0] = out_2;
  //   Shamt[4:0] = out_2[10:6]; Rd[4:0] = out_2[15:11]; Rt[4:0] = out_2[20:16]; Rs[4:0] = out_2[25:21];
  //   OpCode[5:0] = out_2[31:26]; MemAddr[31:0] = out_8; MemData[31:0] = out_9; pc[31:0] = out_3;
  //   RegAddr[4:0] = out_5; RegData[31:0] = out_6; RegWE = out_4; rst = in_1
endmodule

module ALU (
  input  [31:0] in1,
  input  [31:0] in2,
  input  [4:0] \type ,
  output [31:0] out,
  output zero
);

  wire beq, bne, comparator_2_eq;
  wire [31:0] add, lui, ori, sll, sub, xori;

  Adder #(.width(32)) adder_1 (.a(in1), .b(in2), .out(add));  // open: cin, cout
  Subtractor #(.width(32)) subtractor_1 (.a(in1), .b(in2), .out(sub));  // open: bin, bout
  assign xori = in1 ^ in2;  // XOR_Gate xor_1, 32 bits wide
  Shifter #(.width(32)) shifter_1 (.in(in2), .\dist (5'b10000), .out(lui));
  Comparator #(.width(32)) comparator_1 (.a(in1), .b(in2), .eq(beq));  // open: gt, lt
  Comparator #(.width(32)) comparator_2 (.a(in1), .b(in2), .eq(comparator_2_eq));  // open: gt, lt
  assign ori = in1 | in2;  // OR_Gate or_1, 32 bits wide
  not not_1 (bne, comparator_2_eq);
  Shifter #(.width(32)) shifter_2 (.in(in2), .\dist (in1[4:0]), .out(sll));
  Multiplexer #(.select(5), .width(32)) multiplexer_1 (
    .in0({32{1'b0}}), .in1(add), .in2(sub), .in3(add), .in4(xori), .in5(lui), .in6(add), .in7(add),
    .in8({32{1'b0}}), .in9({32{1'b0}}), .in10({32{1'b0}}), .in11({32{1'b0}}), .in12({32{1'b0}}),
    .in13({32{1'b0}}), .in14(ori), .in15(sll), .in16(sll), .out(out), .sel(\type ));  // open: in17, in18, in19, in20, in21, in22, in23, in24, in25, in26, in27, in28, in29, in30, in31, en
  Multiplexer #(.select(5)) multiplexer_2 (
    .in8(beq), .in9(bne), .out(zero), .sel(\type ));  // open: in0, in1, in2, in3, in4, in5, in6, in7, in10, in11, in12, in13, in14, in15, in16, in17, in18, in19, in20, in21, in22, in23, in24, in25, in26, in27, in28, in29, in30, in31, en

  // Other names for the same wires on the sheet: sllv[31:0] = sll; addiu[31:0] = add; lw[31:0] = add; sw[31:0] = add
endmodule

module PC (
  input  [31:0] nextPC,
  input  clk,
  input  rst,
  output [31:0] PC
);

  wire [31:0] register_1_q, xor_1_out;

  assign xor_1_out = 32'h3000 ^ nextPC;  // XOR_Gate xor_1, 32 bits wide
  Register #(.width(32)) register_1 (.D(xor_1_out), .Q(register_1_q), .clk(clk), .clr(rst));  // open: en
  assign PC = 32'h3000 ^ register_1_q;  // XOR_Gate xor_2, 32 bits wide
endmodule

module nextPC (
  input  [31:0] PC,
  input  [31:0] GRF,
  input  [25:0] imm26,
  input  [15:0] imm16,
  input  zero,
  input  [1:0] nextPC_Sel,
  output [31:0] next_PC
);

  wire [31:0] adder_2_out, bit_extender_1_out, multiplexer_1_out, PC_4;

  assign bit_extender_1_out = {{14{imm16[15]}}, {imm16, 2'b00}};  // Bit_Extender bit_extender_1
  Adder #(.width(32)) adder_1 (.a(PC), .b(32'h4), .out(PC_4));  // open: cin, cout
  Adder #(.width(32)) adder_2 (.a(PC_4), .b(bit_extender_1_out), .out(adder_2_out));  // open: cin, cout
  Multiplexer #(.width(32)) multiplexer_1 (
    .in0(PC_4), .in1(adder_2_out), .out(multiplexer_1_out), .sel(zero));  // open: en
  Multiplexer #(.select(2), .width(32)) multiplexer_2 (
    .in0(PC_4), .in1(GRF), .in2({PC[31:28], imm26, 2'b00}), .in3(multiplexer_1_out), .out(next_PC),
    .sel(nextPC_Sel));  // open: en
endmodule

module IM (
  input  [31:0] PC_Addr,
  output [31:0] out_2
);

  wire [31:0] subtractor_1_out;

  Subtractor #(.width(32)) subtractor_1 (.a(PC_Addr), .b(32'h3000), .out(subtractor_1_out));  // open: bin, bout
  ROM #(.addrWidth(12), .dataWidth(32)) rom_1 (.addr(subtractor_1_out[13:2]), .data(out_2));  // open: sel

  // Notes on the sheet:
  //   contents of rom_1 (hex, n*v repeats v):
  //   3404007b 348501c8 3c06007b 3c07ffff 34e7ffff 868020 878820 e79020 34080000 ad040000 ad050004
  //   ad060008 ad07000c ad100010 ad110014 ad120018 8d040000 8d05000c ad04001c ad050020 34040001 34050002
  //   34060001 10850001 10860001 ad040024 ad050028
endmodule

module IFU (
  input  [31:0] GRF,
  input  in_2,
  input  in_3,
  input  [25:0] imm26,
  input  [15:0] imm16,
  input  [1:0] select,
  input  zero,
  output [31:0] out_8,
  output [31:0] out_9,
  output [31:0] out_10
);

  wire [31:0] nextpc_1_next_pc;

  nextPC nextpc_1 (
    .PC(out_8), .GRF(GRF), .imm26(imm26), .imm16(imm16), .zero(zero), .nextPC_Sel(select),
    .next_PC(nextpc_1_next_pc));
  PC pc_1 (.nextPC(nextpc_1_next_pc), .clk(in_2), .PC(out_8), .rst(in_3));
  Adder #(.width(32)) adder_1 (.a(out_8), .b(32'h4), .out(out_10));  // open: cin, cout
  IM im_1 (.PC_Addr(out_8), .out_2(out_9));
endmodule

module GRF (
  input  clk,
  input  reset,
  input  WE,
  input  [4:0] A1,
  input  [4:0] A2,
  input  [4:0] A3,
  input  [31:0] WD,
  output [31:0] RD1,
  output [31:0] RD2
);

  wire [31:0] _0, _1, _2, _3, _4, _5, _6, _7, _8, _9, _10, _11, _12, _13, _14, _15, _16, _17, _18, _19, _20,
       _21, _22, _23, _24, _25, _26, _27, _28, _29, _30, _31, w0, w1, w2, w3, w4, w5, w6, w7, w8, w9, w10,
       w11, w12, w13, w14, w15, w16, w17, w18, w19, w20, w21, w22, w23, w24, w25, w26, w27, w28, w29, w30,
       w31;

  Demultiplexer #(.select(5), .width(32), .tristate("true")) demultiplexer_1 (
    .out0(w0), .out1(w1), .out2(w2), .out3(w3), .out4(w4), .out5(w5), .out6(w6), .out7(w7), .out8(w8),
    .out9(w9), .out10(w10), .out11(w11), .out12(w12), .out13(w13), .out14(w14), .out15(w15), .out16(w16),
    .out17(w17), .out18(w18), .out19(w19), .out20(w20), .out21(w21), .out22(w22), .out23(w23), .out24(w24),
    .out25(w25), .out26(w26), .out27(w27), .out28(w28), .out29(w29), .out30(w30), .out31(w31), .in(WD),
    .sel(A3));  // open: en
  Register #(.width(32)) register_1 (.D(w0), .en(1'b0), .Q(_0), .clk(clk), .clr(reset));
  Register #(.width(32)) register_2 (.D(w1), .en(WE), .Q(_1), .clk(clk), .clr(reset));
  Register #(.width(32)) register_3 (.D(w2), .en(WE), .Q(_2), .clk(clk), .clr(reset));
  Register #(.width(32)) register_4 (.D(w3), .en(WE), .Q(_3), .clk(clk), .clr(reset));
  Register #(.width(32)) register_5 (.D(w4), .en(WE), .Q(_4), .clk(clk), .clr(reset));
  Register #(.width(32)) register_6 (.D(w5), .en(WE), .Q(_5), .clk(clk), .clr(reset));
  Register #(.width(32)) register_7 (.D(w6), .en(WE), .Q(_6), .clk(clk), .clr(reset));
  Register #(.width(32)) register_8 (.D(w7), .en(WE), .Q(_7), .clk(clk), .clr(reset));
  Multiplexer #(.select(5), .width(32)) multiplexer_1 (
    .in0(_0), .in1(_1), .in2(_2), .in3(_3), .in4(_4), .in5(_5), .in6(_6), .in7(_7), .in8(_8), .in9(_9),
    .in10(_10), .in11(_11), .in12(_12), .in13(_13), .in14(_14), .in15(_15), .in16(_16), .in17(_17),
    .in18(_18), .in19(_19), .in20(_20), .in21(_21), .in22(_22), .in23(_23), .in24(_24), .in25(_25),
    .in26(_26), .in27(_27), .in28(_28), .in29(_29), .in30(_30), .in31(_31), .out(RD1), .sel(A1));  // open: en
  Register #(.width(32)) register_9 (.D(w8), .en(WE), .Q(_8), .clk(clk), .clr(reset));
  Register #(.width(32)) register_10 (.D(w9), .en(WE), .Q(_9), .clk(clk), .clr(reset));
  Register #(.width(32)) register_11 (.D(w10), .en(WE), .Q(_10), .clk(clk), .clr(reset));
  Register #(.width(32)) register_12 (.D(w11), .en(WE), .Q(_11), .clk(clk), .clr(reset));
  Register #(.width(32)) register_13 (.D(w12), .en(WE), .Q(_12), .clk(clk), .clr(reset));
  Register #(.width(32)) register_14 (.D(w13), .en(WE), .Q(_13), .clk(clk), .clr(reset));
  Register #(.width(32)) register_15 (.D(w14), .en(WE), .Q(_14), .clk(clk), .clr(reset));
  Register #(.width(32)) register_16 (.D(w15), .en(WE), .Q(_15), .clk(clk), .clr(reset));
  Register #(.width(32)) register_17 (.D(w16), .en(WE), .Q(_16), .clk(clk), .clr(reset));
  Register #(.width(32)) register_18 (.D(w17), .en(WE), .Q(_17), .clk(clk), .clr(reset));
  Register #(.width(32)) register_19 (.D(w18), .en(WE), .Q(_18), .clk(clk), .clr(reset));
  Register #(.width(32)) register_20 (.D(w19), .en(WE), .Q(_19), .clk(clk), .clr(reset));
  Register #(.width(32)) register_21 (.D(w20), .en(WE), .Q(_20), .clk(clk), .clr(reset));
  Register #(.width(32)) register_22 (.D(w21), .en(WE), .Q(_21), .clk(clk), .clr(reset));
  Register #(.width(32)) register_23 (.D(w22), .en(WE), .Q(_22), .clk(clk), .clr(reset));
  Register #(.width(32)) register_24 (.D(w23), .en(WE), .Q(_23), .clk(clk), .clr(reset));
  Register #(.width(32)) register_25 (.D(w24), .en(WE), .Q(_24), .clk(clk), .clr(reset));
  Register #(.width(32)) register_26 (.D(w25), .en(WE), .Q(_25), .clk(clk), .clr(reset));
  Register #(.width(32)) register_27 (.D(w26), .en(WE), .Q(_26), .clk(clk), .clr(reset));
  Register #(.width(32)) register_28 (.D(w27), .en(WE), .Q(_27), .clk(clk), .clr(reset));
  Register #(.width(32)) register_29 (.D(w28), .en(WE), .Q(_28), .clk(clk), .clr(reset));
  Register #(.width(32)) register_30 (.D(w29), .en(WE), .Q(_29), .clk(clk), .clr(reset));
  Register #(.width(32)) register_31 (.D(w30), .en(WE), .Q(_30), .clk(clk), .clr(reset));
  Register #(.width(32)) register_32 (.D(w31), .en(WE), .Q(_31), .clk(clk), .clr(reset));
  Multiplexer #(.select(5), .width(32)) multiplexer_2 (
    .in0(_0), .in1(_1), .in2(_2), .in3(_3), .in4(_4), .in5(_5), .in6(_6), .in7(_7), .in8(_8), .in9(_9),
    .in10(_10), .in11(_11), .in12(_12), .in13(_13), .in14(_14), .in15(_15), .in16(_16), .in17(_17),
    .in18(_18), .in19(_19), .in20(_20), .in21(_21), .in22(_22), .in23(_23), .in24(_24), .in25(_25),
    .in26(_26), .in27(_27), .in28(_28), .in29(_29), .in30(_30), .in31(_31), .out(RD2), .sel(A2));  // open: en

  // Other names for the same wires on the sheet: rst = reset
endmodule

module Controller (
  input  [5:0] Funct,
  input  [5:0] OpCode,
  output [1:0] nextPC_Sel,
  output RegWriteEnable,
  output ALUInput2,
  output ExtOp,
  output RegDst,
  output DM_WE,
  output MemtoReg,
  output PCtoReg,
  output Reg_ra,
  output ALUInput1,
  output [4:0] \type 
);

  wire add, addiu, beq, bne, comparator_1_eq, comparator_12_eq, comparator_13_eq, comparator_14_eq,
       comparator_15_eq, comparator_16_eq, comparator_17_eq, comparator_18_eq, comparator_19_eq, j, jal,
       jalr, jr, lui, lw, ori, priority_encoder_1_gs, sll, sllv, sub, sw, xori;
  wire [4:0] priority_encoder_1_out;

  Multiplexer #(.width(5)) multiplexer_1 (
    .in0({5{1'b0}}), .in1(priority_encoder_1_out), .out(\type ), .sel(priority_encoder_1_gs));  // open: en
  Priority_Encoder #(.select(5)) priority_encoder_1 (
    .in1(add), .in2(sub), .in3(addiu), .in4(xori), .in5(lui), .in6(lw), .in7(sw), .in8(beq), .in9(bne),
    .in10(j), .in11(jal), .in12(jr), .in13(jalr), .in14(ori), .in15(sll), .in16(sllv),
    .out(priority_encoder_1_out), .gs(priority_encoder_1_gs));  // open: in0, in17, in18, in19, in20, in21, in22, in23, in24, in25, in26, in27, in28, in29, in30, in31, en_out, en_in
  Comparator #(.width(6)) comparator_1 (.a(OpCode), .b({6{1'b0}}), .eq(comparator_1_eq));  // open: gt, lt
  Comparator #(.width(6)) comparator_2 (.a(OpCode), .b(6'b001001), .eq(addiu));  // open: gt, lt
  Comparator #(.width(6)) comparator_3 (.a(OpCode), .b(6'b001110), .eq(xori));  // open: gt, lt
  Comparator #(.width(6)) comparator_4 (.a(OpCode), .b(6'b001111), .eq(lui));  // open: gt, lt
  Comparator #(.width(6)) comparator_5 (.a(OpCode), .b(6'b100011), .eq(lw));  // open: gt, lt
  Comparator #(.width(6)) comparator_6 (.a(OpCode), .b(6'b101011), .eq(sw));  // open: gt, lt
  Comparator #(.width(6)) comparator_7 (.a(OpCode), .b(6'b000100), .eq(beq));  // open: gt, lt
  Comparator #(.width(6)) comparator_8 (.a(OpCode), .b(6'b000101), .eq(bne));  // open: gt, lt
  Comparator #(.width(6)) comparator_9 (.a(OpCode), .b(6'b000010), .eq(j));  // open: gt, lt
  Comparator #(.width(6)) comparator_10 (.a(OpCode), .b(6'b000011), .eq(jal));  // open: gt, lt
  Comparator #(.width(6)) comparator_11 (.a(OpCode), .b(6'b001101), .eq(ori));  // open: gt, lt
  Multiplexer #(.select(5), .width(2)) multiplexer_2 (
    .in0(2'b00), .in1(2'b00), .in2(2'b00), .in3(2'b00), .in4(2'b00), .in5(2'b00), .in6(2'b00), .in7(2'b00),
    .in8(2'b11), .in9(2'b11), .in10(2'b10), .in11(2'b10), .in12(2'b01), .in13(2'b01), .in14(2'b00),
    .in15(2'b00), .in16(2'b00), .out(nextPC_Sel), .sel(\type ));  // open: in17, in18, in19, in20, in21, in22, in23, in24, in25, in26, in27, in28, in29, in30, in31, en
  Multiplexer #(.select(5)) multiplexer_3 (
    .in0(1'b0), .in1(1'b1), .in2(1'b1), .in3(1'b1), .in4(1'b1), .in5(1'b1), .in6(1'b1), .in7(1'b0),
    .in8(1'b0), .in9(1'b0), .in10(1'b0), .in11(1'b1), .in12(1'b0), .in13(1'b1), .in14(1'b1), .in15(1'b1),
    .in16(1'b1), .out(RegWriteEnable), .sel(\type ));  // open: in17, in18, in19, in20, in21, in22, in23, in24, in25, in26, in27, in28, in29, in30, in31, en
  Comparator #(.width(6)) comparator_12 (.a(Funct), .b(6'b100000), .eq(comparator_12_eq));  // open: gt, lt
  Comparator #(.width(6)) comparator_13 (.a(Funct), .b(6'b100010), .eq(comparator_13_eq));  // open: gt, lt
  Comparator #(.width(6)) comparator_14 (.a(Funct), .b(6'b001000), .eq(comparator_14_eq));  // open: gt, lt
  Comparator #(.width(6)) comparator_15 (.a(Funct), .b(6'b001001), .eq(comparator_15_eq));  // open: gt, lt
  Comparator #(.width(6)) comparator_16 (.a(Funct), .b({6{1'b0}}), .eq(comparator_16_eq));  // open: gt, lt
  Comparator #(.width(6)) comparator_17 (.a(Funct), .b(6'b000100), .eq(comparator_17_eq));  // open: gt, lt
  Comparator #(.width(6)) comparator_18 (.a(Funct), .eq(comparator_18_eq));  // open: b, gt, lt
  Comparator #(.width(6)) comparator_19 (.a(Funct), .eq(comparator_19_eq));  // open: b, gt, lt
  and u_add (add, comparator_12_eq, comparator_1_eq);
  and u_sub (sub, comparator_13_eq, comparator_1_eq);
  and u_jr (jr, comparator_14_eq, comparator_1_eq);
  and u_jalr (jalr, comparator_15_eq, comparator_1_eq);
  and u_sll (sll, comparator_16_eq, comparator_1_eq);
  and u_sllv (sllv, comparator_17_eq, comparator_1_eq);
  // AND_Gate and_1 has open pins: in0=comparator_18_eq, in1=comparator_1_eq, out=open
  // AND_Gate and_2 has open pins: in0=comparator_19_eq, in1=comparator_1_eq, out=open
  Multiplexer #(.select(5)) multiplexer_4 (
    .in0(1'b0), .in1(1'b0), .in2(1'b0), .in3(1'b1), .in4(1'b1), .in5(1'b1), .in6(1'b1), .in7(1'b1),
    .in8(1'b0), .in9(1'b0), .in10(1'b0), .in11(1'b0), .in12(1'b0), .in13(1'b0), .in14(1'b1), .in15(1'b0),
    .in16(1'b0), .out(ALUInput2), .sel(\type ));  // open: in17, in18, in19, in20, in21, in22, in23, in24, in25, in26, in27, in28, in29, in30, in31, en
  Multiplexer #(.select(5)) multiplexer_5 (
    .in0(1'b0), .in1(1'b0), .in2(1'b0), .in3(1'b1), .in4(1'b0), .in5(1'b0), .in6(1'b1), .in7(1'b1),
    .in8(1'b0), .in9(1'b0), .in10(1'b0), .in11(1'b0), .in12(1'b0), .in13(1'b0), .in14(1'b0), .in15(1'b0),
    .in16(1'b0), .out(ExtOp), .sel(\type ));  // open: in17, in18, in19, in20, in21, in22, in23, in24, in25, in26, in27, in28, in29, in30, in31, en
  Multiplexer #(.select(5)) multiplexer_6 (
    .in0(1'b0), .in1(1'b0), .in2(1'b0), .in3(1'b1), .in4(1'b1), .in5(1'b1), .in6(1'b1), .in7(1'b1),
    .in8(1'b1), .in9(1'b1), .in10(1'b1), .in11(1'b1), .in12(1'b1), .in13(1'b0), .in14(1'b1), .in15(1'b0),
    .in16(1'b0), .out(RegDst), .sel(\type ));  // open: in17, in18, in19, in20, in21, in22, in23, in24, in25, in26, in27, in28, in29, in30, in31, en
  Multiplexer #(.select(5)) multiplexer_7 (
    .in0(1'b0), .in1(1'b0), .in2(1'b0), .in3(1'b0), .in4(1'b0), .in5(1'b0), .in6(1'b0), .in7(1'b1),
    .in8(1'b0), .in9(1'b0), .in10(1'b0), .in11(1'b0), .in12(1'b0), .in13(1'b0), .in14(1'b0), .in15(1'b0),
    .in16(1'b0), .out(DM_WE), .sel(\type ));  // open: in17, in18, in19, in20, in21, in22, in23, in24, in25, in26, in27, in28, in29, in30, in31, en
  Multiplexer #(.select(5)) multiplexer_8 (
    .in0(1'b0), .in1(1'b0), .in2(1'b0), .in3(1'b0), .in4(1'b0), .in5(1'b0), .in6(1'b1), .in7(1'b0),
    .in8(1'b0), .in9(1'b0), .in10(1'b0), .in11(1'b0), .in12(1'b0), .in13(1'b0), .in14(1'b0), .in15(1'b0),
    .in16(1'b0), .out(MemtoReg), .sel(\type ));  // open: in17, in18, in19, in20, in21, in22, in23, in24, in25, in26, in27, in28, in29, in30, in31, en
  Multiplexer #(.select(5)) multiplexer_9 (
    .in0(1'b0), .in1(1'b0), .in2(1'b0), .in3(1'b0), .in4(1'b0), .in5(1'b0), .in6(1'b0), .in7(1'b0),
    .in8(1'b0), .in9(1'b0), .in10(1'b0), .in11(1'b1), .in12(1'b0), .in13(1'b1), .in14(1'b0), .in15(1'b0),
    .in16(1'b0), .out(PCtoReg), .sel(\type ));  // open: in17, in18, in19, in20, in21, in22, in23, in24, in25, in26, in27, in28, in29, in30, in31, en
  Multiplexer #(.select(5)) multiplexer_10 (
    .in0(1'b0), .in1(1'b0), .in2(1'b0), .in3(1'b0), .in4(1'b0), .in5(1'b0), .in6(1'b0), .in7(1'b0),
    .in8(1'b0), .in9(1'b0), .in10(1'b0), .in11(1'b1), .in12(1'b0), .in13(1'b0), .in14(1'b0), .in15(1'b0),
    .in16(1'b0), .out(Reg_ra), .sel(\type ));  // open: in17, in18, in19, in20, in21, in22, in23, in24, in25, in26, in27, in28, in29, in30, in31, en
  Multiplexer #(.select(5)) multiplexer_11 (
    .in0(1'b0), .in1(1'b0), .in2(1'b0), .in3(1'b0), .in4(1'b0), .in5(1'b0), .in6(1'b0), .in7(1'b0),
    .in8(1'b0), .in9(1'b0), .in10(1'b0), .in11(1'b0), .in12(1'b0), .in13(1'b0), .in14(1'b0), .in15(1'b1),
    .in16(1'b0), .out(ALUInput1), .sel(\type ));  // open: in17, in18, in19, in20, in21, in22, in23, in24, in25, in26, in27, in28, in29, in30, in31, en
endmodule

module Ext (
  input  [15:0] imm16,
  input  Op,
  output [31:0] imm32
);

  wire [31:0] bit_extender_1_out, bit_extender_2_out;

  assign bit_extender_1_out = {{16{1'b0}}, imm16};  // Bit_Extender bit_extender_1
  assign bit_extender_2_out = {{16{imm16[15]}}, imm16};  // Bit_Extender bit_extender_2
  Multiplexer #(.width(32)) multiplexer_1 (
    .in0(bit_extender_1_out), .in1(bit_extender_2_out), .out(imm32), .sel(Op));  // open: en
endmodule

module ImmExt (
  input  [31:0] Instr,
  input  Op,
  output [31:0] imm32,
  output [15:0] imm16
);

  Ext ext_1 (.imm16(Instr[15:0]), .Op(Op), .imm32(imm32));

  assign imm16 = Instr[15:0];
endmodule

module DM (
  input  [31:0] Addr,
  input  [31:0] WriteData,
  input  WriteEnable,
  input  clk,
  input  rst,
  output [31:0] Data
);

  RAM #(.addrWidth(16), .dataWidth(32), .bus("separate")) ram_1 (
    .addr(Addr[17:2]), .din(WriteData), .data(Data), .str(WriteEnable), .clk(clk), .clr(rst));  // open: sel, ld
endmodule

module RegWE (
  input  in_1,
  input  [4:0] in_2,
  input  [4:0] in_3,
  input  [4:0] in_4,
  input  [4:0] in_5,
  input  [4:0] in_6,
  output out_7
);

  wire and_1_out, comparator_1_eq, comparator_2_eq, comparator_3_eq, comparator_4_eq, not_1_out;

  Comparator #(.width(5)) comparator_1 (.a(in_3), .b({5{1'b0}}), .eq(comparator_1_eq));  // open: gt, lt
  Comparator #(.width(5)) comparator_2 (.a(in_4), .b({5{1'b0}}), .eq(comparator_2_eq));  // open: gt, lt
  Comparator #(.width(5)) comparator_3 (.a(in_5), .b({5{1'b0}}), .eq(comparator_3_eq));  // open: gt, lt
  Comparator #(.width(5)) comparator_4 (.a(in_6), .b(5'b01111), .eq(comparator_4_eq));  // open: gt, lt
  not not_1 (not_1_out, and_1_out);
  and and_1 (and_1_out, comparator_1_eq, comparator_2_eq, comparator_3_eq, comparator_4_eq);
  and and_2 (out_7, in_1, not_1_out);

  // Other names for the same wires on the sheet: Controller_RegWE = in_1; Rd[4:0] = in_4; Rs[4:0] = in_2;
  //   Rt[4:0] = in_3; Shamt[4:0] = in_5; type[4:0] = in_6
endmodule
